// Logisim project hw_4.circ as structural Verilog: 4 circuits, main circuit top
module top (
  input  A0,
  input  B0,
  input  A1,
  input  B1,
  input  A2,
  input  B2,
  input  A3,
  input  B3,
  output S0,
  output S1,
  output S2,
  output S3
);

  wire adder_1_g, adder_1_p, adder_2_g, adder_2_p, adder_3_g, adder_3_p, adder_4_g, adder_4_p,
       carry_chain_1_co, carry_chain_2_co, carry_chain_3_co;

  adder adder_1 (.A(A0), .B(B0), .G(adder_1_g), .P(adder_1_p), .S(S0), .CI(1'b0));
  carry_chain carry_chain_1 (.G(adder_1_g), .P(1'b0), .CI(adder_1_p), .CO(carry_chain_1_co));
  adder adder_2 (.A(A1), .B(B1), .G(adder_2_g), .P(adder_2_p), .S(S1), .CI(carry_chain_1_co));
  carry_chain carry_chain_2 (.G(adder_2_g), .P(carry_chain_1_co), .CI(adder_2_p), .CO(carry_chain_2_co));
  adder adder_3 (.A(A2), .B(B2), .G(adder_3_g), .P(adder_3_p), .S(S2), .CI(carry_chain_2_co));
  carry_chain carry_chain_3 (.G(adder_3_g), .P(carry_chain_2_co), .CI(adder_3_p), .CO(carry_chain_3_co));
  adder adder_4 (.A(A3), .B(B3), .G(adder_4_g), .P(adder_4_p), .S(S3), .CI(carry_chain_3_co));
  carry_chain carry_chain_4 (.G(adder_4_g), .P(carry_chain_3_co), .CI(adder_4_p));  // open: CO
endmodule

module carry_chain (
  input  G,
  input  P,
  input  CI,
  output CO
);

  wire nand_1_out, not_1_out;

  not not_1 (not_1_out, G);
  nand nand_1 (nand_1_out, P, CI);
  nand nand_2 (CO, not_1_out, nand_1_out);
endmodule

module adder (
  input  CI,
  input  A,
  input  B,
  output S,
  output G,
  output P
);

  Adder #(.width(1)) adder_1 (.a(A), .b(B), .out(S), .cin(CI));  // open: cout
  and and_1 (G, A, B);
  xor xor_1 (P, A, B);
endmodule

module carry_chain_tl (
  input  CLK,
  input  nCLK,
  input  P,
  input  G,
  input  CI,
  input  CO
);

  wire transistor_1_out, transistor_3_out, transistor_4_out, transistor_5_out, transistor_6_out;

  Transistor transistor_1 (.in(1'b1), .out(transistor_1_out), .gate(CLK));
  Transistor #(.\type ("n")) transistor_2 (.in(transistor_3_out), .out(transistor_1_out), .gate(P));
  Transistor #(.\type ("n")) transistor_3 (.in(transistor_4_out), .out(transistor_3_out), .gate(CI));
  Transistor #(.\type ("n")) transistor_4 (.in(1'b0), .out(transistor_4_out), .gate(CLK));
  Transistor transistor_5 (.in(1'b1), .out(transistor_5_out), .gate(nCLK));
  Transistor transistor_6 (.in(1'b1), .out(transistor_6_out), .gate(G));
  Transistor #(.\type ("n")) transistor_7 (.in(1'b0), .out(transistor_6_out), .gate(G));
  Transistor #(.gate("br")) transistor_8 (.in(transistor_5_out), .out(CO), .gate(transistor_1_out));
  Transistor transistor_9 (.in(transistor_5_out), .out(CO), .gate(transistor_6_out));
  Transistor #(.\type ("n")) transistor_10 (.in(1'b0), .out(CO), .gate(nCLK));
endmodule
