// Logisim project vlsi.circ as structural Verilog: 7 circuits, main circuit comparator
// comp
module comparator (
  input  a,
  input  b,
  input  q_i,
  input  a_2,
  input  b_2,
  input  sel,
  output q_o,
  output min
);

  wire nand_1_out, nand_2_out, nand_3_out, nand_4_out, nand_5_out, not_1_out, not_2_out;

  not not_1 (not_1_out, a);
  not not_2 (not_2_out, sel);
  nand nand_1 (nand_1_out, not_1_out, q_i);
  nand nand_2 (nand_2_out, not_1_out, b);
  nand nand_3 (nand_3_out, b, q_i);
  nand nand_4 (nand_4_out, b_2, not_2_out);
  nand nand_5 (nand_5_out, a_2, sel);
  nand nand_6 (q_o, nand_1_out, nand_2_out, nand_3_out);
  nand nand_7 (min, nand_4_out, nand_5_out);

  // Notes on the sheet:
  //   COMPARATOR
  //   MUX
endmodule

module _3_bit_slice (
  input  q_i,
  input  a_0,
  input  b_0,
  input  a_1,
  input  b_1,
  input  a_2,
  input  b_2,
  output q_o
);

  wire comparator_1_q_o, comparator_2_q_o;

  comparator comparator_1 (.b(a_0), .q_i(b_0), .a_2(q_i), .q_o(comparator_1_q_o));  // open: a, b_2, sel, min
  comparator comparator_2 (
    .b(a_1), .q_i(b_1), .a_2(comparator_1_q_o), .q_o(comparator_2_q_o));  // open: a, b_2, sel, min
  comparator comparator_3 (.b(a_2), .q_i(b_2), .a_2(comparator_2_q_o), .q_o(q_o));  // open: a, b_2, sel, min
endmodule

module mux (
  input  a,
  input  b,
  input  sel,
  output min
);

  wire nand_1_out, nand_2_out, not_1_out;

  not not_1 (not_1_out, sel);
  nand nand_1 (nand_1_out, b, not_1_out);
  nand nand_2 (nand_2_out, a, sel);
  nand nand_3 (min, nand_1_out, nand_2_out);
endmodule

module main (
  input  q_i,
  input  a_0,
  input  b_0,
  input  a_1,
  input  b_1,
  input  a_2,
  input  b_2,
  output q_o,
  output out_9,
  output out_10,
  output out_11
);

  wire comparator_1_q_o, comparator_2_q_o;

  comparator comparator_1 (.b(a_0), .q_i(b_0), .a_2(q_i), .sel(q_o), .q_o(comparator_1_q_o));  // open: a, b_2, min
  mux mux_1 (.a(a_0), .b(b_0), .sel(q_o), .min(out_9));
  comparator comparator_2 (
    .b(a_1), .q_i(b_1), .a_2(comparator_1_q_o), .sel(q_o), .q_o(comparator_2_q_o));  // open: a, b_2, min
  mux mux_2 (.a(a_1), .b(b_1), .sel(q_o), .min(out_10));
  comparator comparator_3 (.b(a_2), .q_i(b_2), .a_2(comparator_2_q_o), .sel(q_o), .q_o(q_o));  // open: a, b_2, min
  mux mux_3 (.a(a_2), .b(b_2), .sel(q_o), .min(out_11));
endmodule

module comp_trans (
  input  a,
  input  b,
  input  q_i,
  output q_o
);

  wire transistor_1_out, transistor_2_out, transistor_3_out, transistor_4_out, transistor_5_out,
       transistor_6_out, transistor_7_out, transistor_18_out, transistor_19_out;

  Transistor #(.\type ("n"), .gate("br")) transistor_1 (.in(1'b0), .out(transistor_1_out), .gate(a));
  Transistor #(.\type ("n"), .gate("br")) transistor_2 (.in(1'b0), .out(transistor_2_out), .gate(transistor_1_out));
  Transistor #(.\type ("n"), .gate("br")) transistor_3 (.in(transistor_2_out), .out(transistor_3_out), .gate(b));
  Transistor #(.\type ("n"), .gate("br")) transistor_4 (.in(1'b0), .out(transistor_4_out), .gate(b));
  Transistor #(.\type ("n"), .gate("br")) transistor_5 (.in(transistor_4_out), .out(transistor_5_out), .gate(q_i));
  Transistor #(.\type ("n"), .gate("br")) transistor_6 (.in(1'b0), .out(transistor_6_out), .gate(q_i));
  Transistor #(.\type ("n"), .gate("br")) transistor_7 (
    .in(transistor_6_out), .out(transistor_7_out), .gate(transistor_1_out));
  Transistor transistor_8 (.in(1'b1), .out(transistor_1_out), .gate(a));
  Transistor transistor_9 (.in(1'b1), .out(transistor_3_out), .gate(transistor_1_out));
  Transistor transistor_10 (.in(1'b1), .out(transistor_3_out), .gate(b));
  Transistor transistor_11 (.in(1'b1), .out(transistor_5_out), .gate(b));
  Transistor transistor_12 (.in(1'b1), .out(transistor_5_out), .gate(q_i));
  Transistor transistor_13 (.in(1'b1), .out(transistor_7_out), .gate(q_i));
  Transistor transistor_14 (.in(1'b1), .out(transistor_7_out), .gate(transistor_1_out));
  Transistor #(.gate("br")) transistor_15 (.in(1'b1), .out(q_o), .gate(transistor_3_out));
  Transistor #(.gate("br")) transistor_16 (.in(1'b1), .out(q_o), .gate(transistor_5_out));
  Transistor #(.gate("br")) transistor_17 (.in(1'b1), .out(q_o), .gate(transistor_7_out));
  Transistor #(.\type ("n")) transistor_18 (.in(1'b0), .out(transistor_18_out), .gate(transistor_3_out));
  Transistor #(.\type ("n")) transistor_19 (.in(transistor_18_out), .out(transistor_19_out), .gate(transistor_5_out));
  Transistor #(.\type ("n")) transistor_20 (.in(transistor_19_out), .out(q_o), .gate(transistor_7_out));
endmodule

module mux_trans (
  input  a,
  input  b,
  input  sel,
  output min
);

  wire transistor_1_out, transistor_2_out, transistor_3_out, transistor_5_out, transistor_6_out,
       transistor_7_out;

  Transistor #(.\type ("n"), .gate("br")) transistor_1 (.in(1'b0), .out(transistor_1_out), .gate(a));
  Transistor #(.\type ("n"), .gate("br")) transistor_2 (.in(transistor_1_out), .out(transistor_2_out), .gate(sel));
  Transistor #(.\type ("n"), .gate("br")) transistor_3 (.in(1'b0), .out(transistor_3_out), .gate(transistor_2_out));
  Transistor #(.\type ("n"), .gate("br")) transistor_4 (.in(transistor_3_out), .out(min), .gate(transistor_6_out));
  Transistor #(.\type ("n"), .gate("br")) transistor_5 (.in(1'b0), .out(transistor_5_out), .gate(b));
  Transistor #(.\type ("n"), .gate("br")) transistor_6 (
    .in(transistor_5_out), .out(transistor_6_out), .gate(transistor_7_out));
  Transistor #(.\type ("n"), .gate("br")) transistor_7 (.in(1'b0), .out(transistor_7_out), .gate(sel));
  Transistor transistor_8 (.in(1'b1), .out(transistor_2_out), .gate(a));
  Transistor transistor_9 (.in(1'b1), .out(transistor_2_out), .gate(sel));
  Transistor transistor_10 (.in(1'b1), .out(min), .gate(transistor_2_out));
  Transistor transistor_11 (.in(1'b1), .out(min), .gate(transistor_6_out));
  Transistor transistor_12 (.in(1'b1), .out(transistor_6_out), .gate(b));
  Transistor transistor_13 (.in(1'b1), .out(transistor_6_out), .gate(transistor_7_out));
  Transistor transistor_14 (.in(1'b1), .out(transistor_7_out), .gate(sel));
endmodule

module test (
  input  a,
  input  b,
  input  a_2,
  input  b_2,
  output out_5,
  output out_6,
  output c
);

  nand nand_1 (out_5, a, b);
  nand nand_2 (out_6, a_2, b_2, c);
  and and_1 (c, a_2, b_2);
endmodule
